# Fritzing sketch triggerbox (saved by Fritzing 0.9.3b)
perfboards: 1

parts:
  Bauteil1 = Arduino Leonardo (Rev3b)
  S1 = Pushbutton [package="[THT]"]
  S2 = Toggle Switch [package=THT]
  RE1 = Rotary Encoder [package=THT]
  R1 = Resistor [tolerance=±5% resistance=10k package=THT]  # not connected
  S3 = Square Pushbutton
  J1 = Power Jack [package=power_jack_smd]
  U1 = RELAY-SOLIDSTATE [package=relay-s108t02]
  LED2 = LED - 5mm [color="Blue (505nm)" package="5 mm [THT]"]
  VCC1 = Battery
  VCC2 = Battery
  J2 = Power Jack [package=power_jack_smd]
  LED3 = LED - 5mm [color="Blue (505nm)" package="5 mm [THT]"]
  R2 = Rotary Potentiometer (Small) [maximum_resistance=50kΩ package=THT]  # not connected
  U2 = 7-SEGMENT-4DIGIT [package=7-segment-4digit]  # not connected
  Power_plug1 = Power plug
  JP1 = Header 2 [package=r_sw_th]
  U3 = MAGJACK-POE [package=magjack-poe]
  S6 = SWITCH-DPDT [package=es]
  R3 = Resistor [tolerance=±5% resistance=100 package=THT]  # not connected
  S7 = Pushbutton [package="[THT]"]
  R4 = Resistor [tolerance=±5% resistance=100 package=THT]  # not connected

nets:
  N1: Bauteil1.D0/RX, U3.RCT
  N2: Bauteil1.D1/TX, U3.TD+
  N3: Bauteil1.D2/SDA, S1.Pin_1, S1.Pin_2, J1.GND
  N4: Bauteil1.D3_PWM/SCL, S6.4
  N5: Bauteil1.D4/A6, S2.L1
  N6: Bauteil1.RESET, S7.Pin_3, S7.Pin_4
  N7: Bauteil1.3V3, U3.RD+
  N8: Bauteil1.GND, S1.Pin_3, S1.Pin_4, J1.GNDBREAK, U1.T1, VCC2.-, S6.3
  N9: Bauteil1.VIN, VCC2.+
  N10: Bauteil1.A0, U3.RD-
  N11: Bauteil1.A1, U3.TD-
  N12: Bauteil1.A3, RE1.EncoderPinB
  N13: Bauteil1.A4, RE1.EncoderPinA
  N14: Bauteil1.D13_PWM, LED2.anode
  N15: S2.COM, U1.T2, LED3.anode
  N16: S3.leg1, J1.PWR
  N17: U1.+, J2.GND
  N18: VCC1.+, S6.5
  N19: Power_plug1.VCC, JP1.1

notes:
  GND
  VIN
  3V
  CLK
  MOSI
  CS
  MISO
  LITE
  w/MicroSD Socket - HXD8357D
  VCC
  SCK
  RESET
  SPI MODE !
  3.5" TFT 320x480 + Touchscreen Breakout Board
  IM2
  D/C
  RST
  Y+
  X+
  Y-
  X-
  IM1
  IM0
  CCS
  CD
  Panel-
  Wire remote trigger
  Barrel jack or Chinch
  Rotary encoder with push btn
  10KOhm
  trigger
  POWER SUPPLY 12V 1.3A
  POWER SUPPLY 30V 8amp
  solid state
  OPEN RELAY LED
  #3
  #4
  #2
  #5
  #6
  DPDT On-On
  SAFETY: DISABLE ALL RELAYS
  Voltmeter 3-30V
  50K Poti: External Voltage adj.
  DC/DC power converter
  OUT: 0-±29V
  IN: 30V
  3.0-10V
  0-60V
  Connector #1: for trigger device #1
  - - - - - - - - - - - - - - - - - - - - - - - - - - - - - - - - - - - - - - - - - - - - - - - - - - - - - - - - - - - - - - - - - - - - - - - -
  - - - - - - - - - - - - - - - - - - - - - - - - - - - - - - - - - - - - - - - - - - - - -
  REPEAT 6x
  OVERRIDE
  MANUAL
  METRO M0
  - - - - - - - - - - - - - - -
  EXPRESS
  (Double pole, double throw)
  230V AC
  240V ROCKER
  #1
  RELAY 5amp
  RJ45: External
  Trigger &
  sensor connection
  MAIN SWITCH
  PINOUT RJ45 SOCKET
  From behind socket and left to right:
  Pin# Ethernet cable color To Arduino...
  1. Brown GND
  2. White and Brown 3.3V
  3. Green 5V
  4. White and Blue A0
  5. Blue RX<#0
  6. White and Green 12V
  7. Orange TX>#1
  8. White and Orange A1
  System LED
  100ohm
  Reset
  3-10VDC    5A 60VDC
  -  +      - +
  notice correct hookup of out pins
